# Fritzing sketch fritzing_scheme (saved by Fritzing 1.0.6)
breadboards: 1

parts:
  ESP = ESP32-S3-DevKitC-1-N8R8-v1 [part_number=ESP32-S3-DevKitC-1-N8R8-v1]
  NRF = NRF24L01
  BME280 = BME280 Breakout
  TFT = 2.8" SPI TFT Module [part_number=MSP2807]

nets:
  VCC: ESP.pin_1, ESP.pin_2, NRF.VCC, BME280.3.3V, TFT.pin1, TFT.pin8
  N1: ESP.pin_4, NRF.CE
  N2: ESP.pin_5, NRF.CSN
  N3: ESP.pin_8, NRF.MOSI
  N4: ESP.pin_9, NRF.MISO
  N5: ESP.pin_12, BME280.SDI/SDA
  N6: ESP.pin_15, BME280.SCK/SCL
  N7: ESP.pin_16, TFT.pin3
  N8: ESP.pin_17, TFT.pin6
  N9: ESP.pin_18, TFT.pin7
  N10: ESP.pin_20, TFT.pin5
  GND: ESP.pin_22, ESP.pin_24, ESP.pin_44, NRF.GND, BME280.GND, TFT.pin2
  N11: ESP.pin_27, TFT.pin4
  N12: ESP.pin_40, NRF.SCK

custom parts:
  ESP32-S3-DevKitC-1-N8R8-v1: ESP32-S3-DevKitC-1-N8R8-v1 This module is 44pins long (2x22) and 11 pins width.
  2.8" SPI TFT Module: A generic 2.8 inch LCD TFT 320x240 display with touchscreen and SD card slot. Uses the ILI9341 controller, like the Adafruit displays of this size uses.
